# Fritzing sketch Project2 (saved by Fritzing 0.9.1b)
breadboards: 1

parts:
  U1 = HC-SR04 [chip_label=IC package="SIP (Single Inline) [THT]"]
  U2 = HC-SR04 [chip_label=IC package="SIP (Single Inline) [THT]"]
  U3 = HC-SR04 [chip_label=IC package="SIP (Single Inline) [THT]"]
  Raspberry_Pi1 = Raspberry Pi B+
  R1 = Resistor [tolerance=±5% resistance=220 package=THT]
  R2 = Resistor [tolerance=±5% resistance=220 package=THT]
  R3 = Resistor [tolerance=±5% resistance=220 package=THT]

nets:
  VCC: U1.Vcc, U2.Vcc, U3.Vcc, Raspberry_Pi1.5V
  N1: U1.Trig, Raspberry_Pi1.GPIO17, R3.Pin_0
  GND: U1.GND, U2.GND, U3.GND, Raspberry_Pi1.GND
  N2: U2.Trig, Raspberry_Pi1.GPIO10
  N3: U2.Echo, R2.Pin_1
  N4: U3.Trig, Raspberry_Pi1.GPIO5
  N5: U3.Echo, R1.Pin_1
  N6: Raspberry_Pi1.GPIO27, R3.Pin_1
  N7: Raspberry_Pi1.GPIO9, R2.Pin_0
  N8: Raspberry_Pi1.GPIO6, R1.Pin_0

custom parts:
  HC-SR04: HC-SR04 ultrasound distance sensor
