# Fritzing sketch Project2 (saved by Fritzing 0.9.1b)
breadboards: 1

parts:
  U1 = HC-SR04 [chip_label=IC package="SIP (Single Inline) [THT]"]
  Raspberry_Pi1 = Raspberry Pi B+
  R3 = Resistor [tolerance=±5% resistance=220 package=THT]
  LED1 = LED - 5mm [color="Red (633nm)" package="5 mm [THT]"]
  LED2 = LED - 5mm [color="Red (633nm)" package="5 mm [THT]"]
  LED3 = LED - 5mm [color="Red (633nm)" package="5 mm [THT]"]
  LED4 = LED - 5mm [color="Red (633nm)" package="5 mm [THT]"]
  LED5 = LED - 5mm [color="Red (633nm)" package="5 mm [THT]"]
  LED6 = LED - 5mm [color="Red (633nm)" package="5 mm [THT]"]
  R4 = Resistor [tolerance=±5% resistance=220 package=THT]
  R5 = Resistor [tolerance=±5% resistance=220 package=THT]
  R6 = Resistor [tolerance=±5% resistance=220 package=THT]
  R7 = Resistor [tolerance=±5% resistance=220 package=THT]
  R8 = Resistor [tolerance=±5% resistance=220 package=THT]
  R9 = Resistor [tolerance=±5% resistance=220 package=THT]

nets:
  VCC: U1.Vcc, Raspberry_Pi1.5V
  N1: U1.Trig, Raspberry_Pi1.GPIO10, R3.Pin_0
  GND: U1.GND, Raspberry_Pi1.GND, R4.Pin_0, R5.Pin_0, R6.Pin_0, R7.Pin_0, R8.Pin_0, R9.Pin_0
  N2: Raspberry_Pi1.GPIO2, LED1.anode
  N3: Raspberry_Pi1.GPIO3, LED2.anode
  N4: Raspberry_Pi1.GPIO4, LED3.anode
  N5: Raspberry_Pi1.GPIO17, LED4.anode
  N6: Raspberry_Pi1.GPIO27, LED5.anode
  N7: Raspberry_Pi1.GPIO22, LED6.anode
  N8: Raspberry_Pi1.GPIO9, R3.Pin_1
  N9: LED1.cathode, R4.Pin_1
  N10: LED2.cathode, R5.Pin_1
  N11: LED3.cathode, R6.Pin_1
  N12: LED4.cathode, R7.Pin_1
  N13: LED5.cathode, R9.Pin_1
  N14: LED6.cathode, R8.Pin_1

custom parts:
  HC-SR04: HC-SR04 ultrasound distance sensor
