# Fritzing sketch breadboard w-push buttons, led, lcd screen (saved by Fritzing 0.9.3b)
breadboards: 1

parts:
  S2 = Pushbutton [package="[SMD]"]
  S3 = Pushbutton [package="[SMD]"]
  S4 = Pushbutton [package="[SMD]"]
  Raspberry_Pi_1 = Raspberry Pi 3 [part_number=RPI-3-V1.2]
  LCD1 = LCD screen  # not connected
  LED1 = LED - 5mm [color="Red (633nm)" package="5 mm [THT]"]
  LED2 = LED - 5mm [color="Red (633nm)" package="5 mm [THT]"]
  LED3 = LED - 5mm [color="Red (633nm)" package="5 mm [THT]"]
  R1 = Resistor [tolerance=±5% resistance=220 package="2512 [SMD]"]
  R2 = Resistor [tolerance=±5% resistance=220 package="2512 [SMD]"]  # not connected
  R3 = Resistor [tolerance=±5% resistance=220 package="2512 [SMD]"]
  R4 = Resistor [tolerance=±5% resistance=220 package="2512 [SMD]"]

nets:
  N1: S2.Pin_1, S2.Pin_2, Raspberry_Pi_1.GPIO21
  N2: S2.Pin_3, S2.Pin_4, S3.Pin_3, S3.Pin_4, S4.Pin_3, S4.Pin_4, Raspberry_Pi_1.5V, R1.Pin_0, R3.Pin_0, R4.Pin_0
  N3: S3.Pin_1, S3.Pin_2, Raspberry_Pi_1.GPIO20
  N4: S4.Pin_1, S4.Pin_2, Raspberry_Pi_1.GPIO16
  N5: Raspberry_Pi_1.GPIO7, LED1.anode
  N6: Raspberry_Pi_1.GPIO8, LED2.anode
  N7: Raspberry_Pi_1.GPIO25, LED3.anode
  N8: LED1.cathode, R3.Pin_1
  N9: LED2.cathode, R4.Pin_1
  N10: LED3.cathode, R1.Pin_1
